# Fritzing sketch CopLeds(FunnyArduinoHelloWorld) (saved by Fritzing 0.9.3b)
breadboards: 1

parts:
  Componente1 = Arduino Uno (Rev3)
  R1 = Resistor [tolerance=±5% resistance=220 power=330 package=THT]
  R2 = Resistor [tolerance=±5% resistance=220 power=330 package=THT]
  LED1 = LED - 5mm [color="Red (633nm)" package="5 mm [THT]"]
  LED2 = LED - 5mm [color="Blue (470nm)" package="5 mm [THT]"]

nets:
  N1: Componente1.D13/SCK, LED1.cathode
  N2: Componente1.D7, LED2.cathode
  N3: Componente1.5V, R1.Pin_1, R2.Pin_1
  N4: R1.Pin_0, LED2.anode
  N5: R2.Pin_0, LED1.anode
