# Fritzing sketch variable_blink_Fritzing (saved by Fritzing 0.9.3b)
breadboards: 1

parts:
  Componente1 = Arduino Uno (Rev3)
  R1 = Rotary Potentiometer (Small) [maximum_resistance=100kΩ package=THT]
  LED1 = LED - 5mm [color="Red (633nm)" package="5 mm [THT]"]

nets:
  N1: Componente1.A0, R1.wiper
  N2: Componente1.D3_PWM, LED1.anode
  N3: Componente1.5V, R1.leg2
  N4: Componente1.GND, R1.leg1, LED1.cathode
